# Fritzing sketch button example (saved by Fritzing 0.9.1b)
breadboards: 1

parts:
  S1 = Pushbutton [package=THT]
  Part1 = Arduino Uno (Rev3)

nets:
  N1: S1.leg0, Part1.GND
  N2: S1.leg1, Part1.D2
