# Fritzing sketch full_circuit (saved by Fritzing 0.9.1b)
breadboards: 1

parts:
  S1 = Pushbutton [package=THT]
  Part1 = Arduino Uno (Rev3)
  J1 = Basic Servo [part_number="sg90 micro servo"]
  J2 = male pin header, 3 pins [form="♂ (male)"]
  J3 = Basic Servo [part_number="Continuous rotation"]
  J4 = male pin header, 3 pins [form="♂ (male)"]
  J5 = Basic Servo [part_number="sg90 micro servo"]
  J6 = male pin header, 3 pins [form="♂ (male)"]
  J7 = Piezo Speaker
  S2 = Reed switch [package=THT]

nets:
  GND: S1.leg0, Part1.GND, J1.gnd, J2.pin1, J3.gnd, J4.pin1, J6.pin1
  N1: S1.leg1, Part1.D2
  N2: Part1.D8, J7.pin2
  N3: Part1.D9_PWM, S2.pin_2
  N4: Part1.D5_PWM, J6.pin3
  N5: Part1.D6_PWM, J3.pulse, J4.pin3
  N6: Part1.D7, J1.pulse, J2.pin3
  VCC: Part1.5V, J1.vcc, J2.pin2, J3.vcc, J4.pin2, J5.vcc, J6.pin2, J7.pin1, S2.pin_1
