# Fritzing sketch servo (saved by Fritzing 0.9.1b)
breadboards: 1

parts:
  S1 = Pushbutton [package=THT]
  Part1 = Arduino Uno (Rev3)
  J1 = Basic Servo
  J2 = male pin header, 3 pins [form="♂ (male)"]

nets:
  GND: S1.leg0, Part1.GND, J1.gnd, J2.pin1
  N1: S1.leg1, Part1.D2
  N2: Part1.D7, J1.pulse, J2.pin3
  5V: Part1.5V, J1.vcc, J2.pin2
